// Logisim project 4 e 8.circ as structural Verilog: 4 circuits, main circuit main
module main (
  input  in_1,
  input  in_2,
  input  in_3,
  input  in_4,
  input  in_5,
  input  in_6,
  input  in_7,
  input  in_8,
  input  in_9,
  input  in_10,
  input  in_11,
  input  in_12,
  input  in_13,
  input  in_14,
  input  in_15,
  input  in_16,
  output out_17,
  output out_18,
  output out_19,
  output out_20,
  output out_21,
  output out_22,
  output out_23,
  output out_24,
  output out_25
);

  somador8bits somador8bits_1 (
    .A4(in_9), .A0(in_1), .B4(in_10), .B0(in_2), .A5(in_11), .A1(in_3), .B5(in_12), .B1(in_4), .A6(in_13),
    .A2(in_5), .B6(in_14), .B2(in_6), .A7(in_15), .A3(in_7), .B7(in_16), .B3(in_8), .C4(out_21), .C0(out_17),
    .C5(out_22), .C1(out_18), .C6(out_23), .C2(out_19), .C7(out_24), .C3(out_20), .cOut(out_25), .in_1(1'b0));
endmodule

module somador1bit (
  input  A0,
  input  A1,
  input  cIn,
  output B0,
  output cOut
);

  wire and_1_out, and_2_out, and_3_out, xor_1_out;

  and and_1 (and_1_out, A0, A1);
  and and_2 (and_2_out, A0, cIn);
  and and_3 (and_3_out, A1, cIn);
  xor xor_1 (xor_1_out, A0, A1);
  or or_1 (cOut, and_1_out, and_2_out, and_3_out);
  xor xor_2 (B0, xor_1_out, cIn);
endmodule

module somador4bits (
  input  B3,
  input  A3,
  input  B2,
  input  A2,
  input  B1,
  input  A1,
  input  cIn,
  input  B0,
  input  A0,
  output cOut,
  output C3,
  output C2,
  output C1,
  output C0
);

  wire somador1bit_2_cout, somador1bit_3_cout, somador1bit_4_cout;

  somador1bit somador1bit_1 (.A0(A3), .A1(B3), .cIn(somador1bit_2_cout), .B0(C3), .cOut(cOut));
  somador1bit somador1bit_2 (.A0(A2), .A1(B2), .cIn(somador1bit_3_cout), .B0(C2), .cOut(somador1bit_2_cout));
  somador1bit somador1bit_3 (.A0(A1), .A1(B1), .cIn(somador1bit_4_cout), .B0(C1), .cOut(somador1bit_3_cout));
  somador1bit somador1bit_4 (.A0(A0), .A1(B0), .cIn(cIn), .B0(C0), .cOut(somador1bit_4_cout));
endmodule

module somador8bits (
  input  in_1,
  input  A4,
  input  A0,
  input  B4,
  input  B0,
  input  A5,
  input  A1,
  input  B5,
  input  B1,
  input  A6,
  input  A2,
  input  B6,
  input  B2,
  input  A7,
  input  A3,
  input  B7,
  input  B3,
  output C4,
  output C0,
  output C5,
  output C1,
  output C6,
  output C2,
  output C7,
  output C3,
  output cOut
);

  wire somador4bits_2_cout;

  somador4bits somador4bits_1 (
    .B3(B7), .A3(A7), .B2(B6), .A2(A6), .B1(B5), .A1(A5), .B0(B4), .A0(A4), .cOut(cOut), .C3(C7), .C2(C6),
    .C1(C5), .C0(C4), .cIn(somador4bits_2_cout));
  somador4bits somador4bits_2 (
    .B3(B3), .A3(A3), .B2(B2), .A2(A2), .B1(B1), .A1(A1), .B0(B0), .A0(A0), .cOut(somador4bits_2_cout),
    .C3(C3), .C2(C2), .C1(C1), .C0(C0), .cIn(in_1));
endmodule
