// Logisim project 1.circ as structural Verilog: 2 circuits, main circuit D
module D (
  input  in_1,
  output out_2,
  output out_3
);

  wire clock_1_out, nand_1_out, nand_2_out;

  Clock clock_1 (.out(clock_1_out));
  nand nand_1 (nand_1_out, in_1, clock_1_out);
  nand nand_2 (nand_2_out, ~in_1, clock_1_out);  // NAND_Gate
  nand nand_3 (out_2, nand_1_out, out_3);
  nand nand_4 (out_3, out_2, nand_2_out);
endmodule

module JK (
  input  in_1,
  input  in_2,
  input  in_3,
  input  in_4,
  output out_5,
  output out_6
);

  wire clock_1_out, nand_1_out, nand_2_out, nand_3_out, nand_4_out, nand_5_out, nand_6_out, not_1_out,
       not_2_out, not_3_out;

  Clock clock_1 (.out(clock_1_out));
  not not_1 (not_1_out, in_1);
  nand nand_1 (nand_1_out, out_6, in_2, clock_1_out);
  not not_2 (not_2_out, clock_1_out);
  nand nand_2 (nand_2_out, clock_1_out, in_3, out_5);
  not not_3 (not_3_out, in_4);
  nand nand_3 (nand_3_out, not_1_out, nand_1_out, nand_4_out);
  nand nand_4 (nand_4_out, nand_3_out, nand_2_out, not_3_out);
  nand nand_5 (nand_5_out, not_3_out, nand_3_out, not_2_out);
  nand nand_6 (nand_6_out, not_2_out, nand_4_out, not_1_out);
  nand nand_7 (out_5, not_1_out, nand_5_out, out_6);
  nand nand_8 (out_6, out_5, nand_6_out, not_3_out);
endmodule
