// Logisim project 10.circ as structural Verilog: 14 circuits, main circuit main
module main (
  input  [7:0] A,
  input  [7:0] B,
  input  [3:0] in_3,
  output [7:0] out_4
);

  wire mux_4_1_out_2, mux_4_1_out_3, mux_4_1_out_4, mux_4_1_out_5, mux_4_1_out_6, mux_4_1_out_7,
       mux_4_1_out_8, mux_4_1_out_9, mux_4_1_out_10, mux_4_1_out_11, mux_4_1_out_12, mux_4_1_out_13,
       mux_4_1_out_14;
  wire [7:0] and_1_out_3, deslocador_d_1_out_2, deslocador_d_2_out_2, deslocador_e_1_out_2,
       deslocador_e_2_out_2, nand_1_out_3, nor_1_out_3, not_1_out_2, not_2_out_2, or_1_out_3,
       somador_8_1_out_3, subtrator_8_1_out_3, xor_1_out_3;

  mux_4 mux_4_1 (
    .in_1(in_3), .out_2(mux_4_1_out_2), .out_3(mux_4_1_out_3), .out_4(mux_4_1_out_4), .out_5(mux_4_1_out_5),
    .out_6(mux_4_1_out_6), .out_7(mux_4_1_out_7), .out_8(mux_4_1_out_8), .out_9(mux_4_1_out_9),
    .out_10(mux_4_1_out_10), .out_11(mux_4_1_out_11), .out_12(mux_4_1_out_12), .out_13(mux_4_1_out_13),
    .out_14(mux_4_1_out_14));
  \and  and_1 (.in_1(A), .in_2(B), .out_3(and_1_out_3));
  \or  or_1 (.in_1(A), .in_2(B), .out_3(or_1_out_3));
  \nand  nand_1 (.in_1(A), .in_2(B), .out_3(nand_1_out_3));
  \nor  nor_1 (.in_1(A), .in_2(B), .out_3(nor_1_out_3));
  \not  not_1 (.in_1(A), .out_2(not_1_out_2));
  \not  not_2 (.in_1(B), .out_2(not_2_out_2));
  \xor  xor_1 (.in_1(A), .in_2(B), .out_3(xor_1_out_3));
  deslocador_D deslocador_d_1 (.in_1(A), .out_2(deslocador_d_1_out_2));
  deslocador_D deslocador_d_2 (.in_1(B), .out_2(deslocador_d_2_out_2));
  deslocador_E deslocador_e_1 (.in_1(A), .out_2(deslocador_e_1_out_2));
  deslocador_E deslocador_e_2 (.in_1(B), .out_2(deslocador_e_2_out_2));
  somador_8 somador_8_1 (.out_3(somador_8_1_out_3), .in_2(A), .in_1(B));
  subtrator_8 subtrator_8_1 (.out_3(subtrator_8_1_out_3), .in_2(A), .in_1(B));
  assign out_4 = mux_4_1_out_2 ? and_1_out_3 : 8'bz;  // Controlled_Buffer controlled_buffer_1
  assign out_4 = mux_4_1_out_3 ? or_1_out_3 : 8'bz;  // Controlled_Buffer controlled_buffer_2
  assign out_4 = mux_4_1_out_4 ? nand_1_out_3 : 8'bz;  // Controlled_Buffer controlled_buffer_3
  assign out_4 = mux_4_1_out_5 ? nor_1_out_3 : 8'bz;  // Controlled_Buffer controlled_buffer_4
  assign out_4 = mux_4_1_out_6 ? not_1_out_2 : 8'bz;  // Controlled_Buffer controlled_buffer_5
  assign out_4 = mux_4_1_out_7 ? not_2_out_2 : 8'bz;  // Controlled_Buffer controlled_buffer_6
  assign out_4 = mux_4_1_out_8 ? xor_1_out_3 : 8'bz;  // Controlled_Buffer controlled_buffer_7
  assign out_4 = mux_4_1_out_9 ? deslocador_d_1_out_2 : 8'bz;  // Controlled_Buffer controlled_buffer_8
  assign out_4 = mux_4_1_out_10 ? deslocador_d_2_out_2 : 8'bz;  // Controlled_Buffer controlled_buffer_9
  assign out_4 = mux_4_1_out_11 ? deslocador_e_1_out_2 : 8'bz;  // Controlled_Buffer controlled_buffer_10
  assign out_4 = mux_4_1_out_12 ? deslocador_e_2_out_2 : 8'bz;  // Controlled_Buffer controlled_buffer_11
  assign out_4 = mux_4_1_out_13 ? somador_8_1_out_3 : 8'bz;  // Controlled_Buffer controlled_buffer_12
  assign out_4 = mux_4_1_out_14 ? subtrator_8_1_out_3 : 8'bz;  // Controlled_Buffer controlled_buffer_13
endmodule

module \and  (
  input  [7:0] in_1,
  input  [7:0] in_2,
  output [7:0] out_3
);

  and and_1 (out_3[7], in_1[7], in_2[7]);
  and and_2 (out_3[6], in_1[6], in_2[6]);
  and and_3 (out_3[5], in_1[5], in_2[5]);
  and and_4 (out_3[3], in_1[3], in_2[3]);
  and and_5 (out_3[4], in_1[4], in_2[4]);
  and and_6 (out_3[2], in_1[2], in_2[2]);
  and and_7 (out_3[0], in_1[0], in_2[0]);
  and and_8 (out_3[1], in_1[1], in_2[1]);
endmodule

module \or  (
  input  [7:0] in_1,
  input  [7:0] in_2,
  output [7:0] out_3
);

  or or_1 (out_3[7], in_1[7], in_2[7]);
  or or_2 (out_3[6], in_1[6], in_2[6]);
  or or_3 (out_3[5], in_1[5], in_2[5]);
  or or_4 (out_3[4], in_1[4], in_2[4]);
  or or_5 (out_3[3], in_1[3], in_2[3]);
  or or_6 (out_3[2], in_1[2], in_2[2]);
  or or_7 (out_3[1], in_1[1], in_2[1]);
  or or_8 (out_3[0], in_1[0], in_2[0]);
endmodule

module \nand  (
  input  [7:0] in_1,
  input  [7:0] in_2,
  output [7:0] out_3
);

  nand nand_1 (out_3[7], in_1[7], in_2[7]);
  nand nand_2 (out_3[6], in_1[6], in_2[6]);
  nand nand_3 (out_3[5], in_1[5], in_2[5]);
  nand nand_4 (out_3[4], in_1[4], in_2[4]);
  nand nand_5 (out_3[3], in_1[3], in_2[3]);
  nand nand_6 (out_3[2], in_1[2], in_2[2]);
  nand nand_7 (out_3[0], in_1[0], in_2[0]);
  nand nand_8 (out_3[1], in_1[1], in_2[1]);
endmodule

module \nor  (
  input  [7:0] in_1,
  input  [7:0] in_2,
  output [7:0] out_3
);

  nor nor_1 (out_3[6], in_1[6], in_2[6]);
  nor nor_2 (out_3[7], in_1[7], in_2[7]);
  nor nor_3 (out_3[5], in_1[5], in_2[5]);
  nor nor_4 (out_3[4], in_1[4], in_2[4]);
  nor nor_5 (out_3[3], in_1[3], in_2[3]);
  nor nor_6 (out_3[2], in_1[2], in_2[2]);
  nor nor_7 (out_3[0], in_1[0], in_2[0]);
  nor nor_8 (out_3[1], in_1[1], in_2[1]);
endmodule

module \not  (
  input  [7:0] in_1,
  output [7:0] out_2
);

  assign out_2 = ~in_1;  // NOT_Gate not_1, 8 bits wide
endmodule

module \xor  (
  input  [7:0] in_1,
  input  [7:0] in_2,
  output [7:0] out_3
);

  xor xor_1 (out_3[7], in_1[7], in_2[7]);
  xor xor_2 (out_3[6], in_1[6], in_2[6]);
  xor xor_3 (out_3[5], in_1[5], in_2[5]);
  xor xor_4 (out_3[3], in_1[3], in_2[3]);
  xor xor_5 (out_3[4], in_1[4], in_2[4]);
  xor xor_6 (out_3[2], in_1[2], in_2[2]);
  xor xor_7 (out_3[1], in_1[1], in_2[1]);
  xor xor_8 (out_3[0], in_1[0], in_2[0]);
endmodule

module deslocador_D (
  input  [7:0] in_1,
  output [7:0] out_2
);


  assign out_2 = {1'b0, in_1[7:1]};
  // also tied to GND on the sheet: in_1[0]
endmodule

module deslocador_E (
  input  [7:0] in_1,
  output [7:0] out_2
);


  assign in_1[6] = in_1[7];
  assign out_2 = {in_1[5:0], 2'b00};
  // also tied to GND on the sheet: in_1[7]
endmodule

module somador (
  input  in_1,
  input  in_2,
  input  in_3,
  output out_4,
  output out_5
);

  wire and_1_out, and_2_out, or_1_out, xor_1_out;

  and and_1 (and_1_out, in_2, in_1);
  or or_1 (or_1_out, in_1, in_2);
  xor xor_1 (xor_1_out, in_1, in_2);
  and and_2 (and_2_out, in_3, or_1_out);
  xor xor_2 (out_4, xor_1_out, in_3);
  or or_2 (out_5, and_1_out, and_2_out);
endmodule

module somador_8 (
  input  [7:0] in_1,
  input  [7:0] in_2,
  output [7:0] out_3
);

  wire somador_1_out_5, somador_2_out_5, somador_3_out_5, somador_4_out_5, somador_5_out_5, somador_6_out_5,
       somador_7_out_5, somador_8_out_5;

  somador somador_1 (.in_1(in_2[0]), .in_2(in_1[0]), .in_3(1'b0), .out_4(out_3[0]), .out_5(somador_1_out_5));
  somador somador_2 (.in_1(in_2[1]), .in_2(in_1[1]), .in_3(somador_1_out_5), .out_4(out_3[1]), .out_5(somador_2_out_5));
  somador somador_3 (.in_1(in_2[2]), .in_2(in_1[2]), .in_3(somador_2_out_5), .out_4(out_3[2]), .out_5(somador_3_out_5));
  somador somador_4 (.in_1(in_2[3]), .in_2(in_1[3]), .in_3(somador_3_out_5), .out_4(out_3[3]), .out_5(somador_4_out_5));
  somador somador_5 (.in_1(in_2[4]), .in_2(in_1[4]), .in_3(somador_4_out_5), .out_4(out_3[4]), .out_5(somador_5_out_5));
  somador somador_6 (.in_1(in_2[5]), .in_2(in_1[5]), .in_3(somador_5_out_5), .out_4(out_3[5]), .out_5(somador_6_out_5));
  somador somador_7 (.in_1(in_2[6]), .in_2(in_1[6]), .in_3(somador_6_out_5), .out_4(out_3[6]), .out_5(somador_7_out_5));
  somador somador_8 (.in_1(in_2[7]), .in_2(in_1[7]), .in_3(somador_7_out_5), .out_4(out_3[7]), .out_5(somador_8_out_5));
  // also tied to GND on the sheet: somador_8_out_5
endmodule

module subtrator (
  input  in_1,
  input  in_2,
  input  in_3,
  output out_4,
  output out_5
);

  wire and_1_out, and_2_out, and_3_out, not_1_out, xor_1_out;

  not not_1 (not_1_out, in_1);
  xor xor_1 (xor_1_out, in_1, in_2);
  and and_1 (and_1_out, not_1_out, in_2);
  and and_2 (and_2_out, not_1_out, in_3);
  and and_3 (and_3_out, in_2, in_3);
  xor xor_2 (out_4, xor_1_out, in_3);
  or or_1 (out_5, and_1_out, and_2_out, and_3_out);
endmodule

module subtrator_8 (
  input  [7:0] in_1,
  input  [7:0] in_2,
  output [7:0] out_3
);

  wire subtrator_1_out_5, subtrator_2_out_5, subtrator_3_out_5, subtrator_4_out_5, subtrator_5_out_5,
       subtrator_6_out_5, subtrator_7_out_5, subtrator_8_out_5;

  subtrator subtrator_1 (.in_1(in_2[0]), .in_2(in_1[0]), .in_3(1'b0), .out_4(out_3[0]), .out_5(subtrator_1_out_5));
  subtrator subtrator_2 (
    .in_1(in_2[1]), .in_2(in_1[1]), .in_3(subtrator_1_out_5), .out_4(out_3[1]), .out_5(subtrator_2_out_5));
  subtrator subtrator_3 (
    .in_1(in_2[2]), .in_2(in_1[2]), .in_3(subtrator_2_out_5), .out_4(out_3[2]), .out_5(subtrator_3_out_5));
  subtrator subtrator_4 (
    .in_1(in_2[3]), .in_2(in_1[3]), .in_3(subtrator_3_out_5), .out_4(out_3[3]), .out_5(subtrator_4_out_5));
  subtrator subtrator_5 (
    .in_1(in_2[4]), .in_2(in_1[4]), .in_3(subtrator_4_out_5), .out_4(out_3[4]), .out_5(subtrator_5_out_5));
  subtrator subtrator_6 (
    .in_1(in_2[5]), .in_2(in_1[5]), .in_3(subtrator_5_out_5), .out_4(out_3[5]), .out_5(subtrator_6_out_5));
  subtrator subtrator_7 (
    .in_1(in_2[6]), .in_2(in_1[6]), .in_3(subtrator_6_out_5), .out_4(out_3[6]), .out_5(subtrator_7_out_5));
  subtrator subtrator_8 (
    .in_1(in_2[7]), .in_2(in_1[7]), .in_3(subtrator_7_out_5), .out_4(out_3[7]), .out_5(subtrator_8_out_5));
  // also tied to GND on the sheet: subtrator_8_out_5
endmodule

module mux_4 (
  input  [3:0] in_1,
  output out_2,
  output out_3,
  output out_4,
  output out_5,
  output out_6,
  output out_7,
  output out_8,
  output out_9,
  output out_10,
  output out_11,
  output out_12,
  output out_13,
  output out_14
);

  and and_1 (out_2, ~in_1[0], ~in_1[1], ~in_1[2], ~in_1[3]);  // AND_Gate
  and and_2 (out_3, in_1[0], ~in_1[1], ~in_1[2], ~in_1[3]);  // AND_Gate
  and and_3 (out_4, ~in_1[0], in_1[1], ~in_1[2], ~in_1[3]);  // AND_Gate
  and and_4 (out_5, in_1[0], in_1[1], ~in_1[2], ~in_1[3]);  // AND_Gate
  and and_5 (out_6, ~in_1[0], ~in_1[1], in_1[2], ~in_1[3]);  // AND_Gate
  and and_6 (out_7, in_1[0], ~in_1[1], in_1[2], ~in_1[3]);  // AND_Gate
  and and_7 (out_8, ~in_1[0], in_1[1], in_1[2], ~in_1[3]);  // AND_Gate
  and and_8 (out_9, in_1[0], in_1[1], in_1[2], ~in_1[3]);  // AND_Gate
  and and_9 (out_10, ~in_1[0], ~in_1[1], ~in_1[2], in_1[3]);  // AND_Gate
  and and_10 (out_11, in_1[0], ~in_1[1], ~in_1[2], in_1[3]);  // AND_Gate
  and and_11 (out_12, ~in_1[0], in_1[1], ~in_1[2], in_1[3]);  // AND_Gate
  and and_12 (out_13, in_1[0], in_1[1], ~in_1[2], in_1[3]);  // AND_Gate
  and and_13 (out_14, ~in_1[0], ~in_1[1], in_1[2], in_1[3]);  // AND_Gate
endmodule
