// Logisim project 12.circ as structural Verilog: 1 circuit, main circuit main
module main (
  input  in_1,
  output out_2
);

  wire and_1_out, and_2_out, clock_1_out, or_1_out;

  and and_1 (and_1_out, ~out_2, in_1);  // AND_Gate
  and and_2 (and_2_out, out_2, ~in_1);  // AND_Gate
  Clock clock_1 (.out(clock_1_out));
  or or_1 (or_1_out, and_1_out, and_2_out);
  D_Flip_Flop d_ff_1 (.clk(clock_1_out), .D(or_1_out), .Q(out_2));  // open: Qn, preset, en, reset
endmodule
