// Logisim project 14.circ as structural Verilog: 1 circuit, main circuit main
module main (
  input  A,
  input  B,
  input  C,
  input  D,
  output out_5
);

  wire and_1_out, and_2_out, and_3_out, and_4_out, and_5_out, and_6_out, or_1_out, or_2_out;

  and and_1 (and_1_out, A, ~B);  // AND_Gate
  and and_2 (and_2_out, ~A, B);  // AND_Gate
  or or_1 (or_1_out, and_1_out, and_2_out);
  and and_3 (and_3_out, or_1_out, ~C);  // AND_Gate
  and and_4 (and_4_out, ~or_1_out, C);  // AND_Gate
  or or_2 (or_2_out, and_3_out, and_4_out);
  and and_5 (and_5_out, or_2_out, ~D);  // AND_Gate
  and and_6 (and_6_out, ~or_2_out, D);  // AND_Gate
  or or_3 (out_5, and_5_out, and_6_out);
endmodule
