// Logisim project 15.circ as structural Verilog: 2 circuits, main circuit main
module main (
  input  [2:0] in_1,
  output out_2
);

  wire and_1_out, and_2_out, and_3_out, and_4_out;

  and and_1 (and_1_out, ~in_1[0], in_1[1], in_1[2]);  // AND_Gate
  and and_2 (and_2_out, in_1[0], ~in_1[1], in_1[2]);  // AND_Gate
  and and_3 (and_3_out, in_1[0], in_1[1], ~in_1[2]);  // AND_Gate
  and and_4 (and_4_out, in_1[0], in_1[1], in_1[2]);
  or or_1 (out_2, and_1_out, and_2_out, and_3_out, and_4_out);

  // Notes on the sheet:
  //   S = A'BC + AB'C + ABC' + ABC
endmodule

module otimizado (
  input  [2:0] in_1,
  output out_2
);

  wire and_1_out, and_2_out, and_3_out;

  and and_1 (and_1_out, in_1[0], in_1[2]);
  and and_2 (and_2_out, in_1[0], in_1[1]);
  and and_3 (and_3_out, in_1[2], in_1[1]);
  or or_1 (out_2, and_1_out, and_2_out, and_3_out);

  // Notes on the sheet:
  //   S = AC + AB + BC
endmodule
