// Logisim project 16.circ as structural Verilog: 8 circuits, main circuit main
module main (
  input  [3:0] in_1
);

  wire a_1_a, b_1_b, c_1_c, d_1_d, e_1_e, f_1_out_2, g_1_g;

  b b_1 (.in_1(in_1), .b(b_1_b));
  a a_1 (.in_1(in_1), .a(a_1_a));
  f f_1 (.in_1(in_1), .out_2(f_1_out_2));
  g g_1 (.in_1(in_1), .g(g_1_g));
  e e_1 (.in_1(in_1), .e(e_1_e));
  d d_1 (.in_1(in_1), .d(d_1_d));
  c c_1 (.in_1(in_1), .c(c_1_c));
  _7_Segment_Display u_7_segment_display_1 (
    .g(g_1_g), .f(f_1_out_2), .a(a_1_a), .b(b_1_b), .e(e_1_e), .d(d_1_d), .c(c_1_c));  // open: dp
endmodule

module a (
  input  [3:0] in_1,
  output a
);

  wire or_1_out, or_2_out;

  or or_1 (or_1_out, in_1[1], in_1[3]);
  or or_2 (or_2_out, ~in_1[1], ~in_1[3]);  // OR_Gate
  and and_1 (a, in_1[0], in_1[2], or_1_out, or_2_out);
endmodule

module b (
  input  [3:0] in_1,
  output b
);

  wire or_1_out, or_2_out;

  or or_1 (or_1_out, ~in_1[2], ~in_1[3]);  // OR_Gate
  or or_2 (or_2_out, in_1[3], in_1[2]);
  and and_1 (b, ~in_1[1], or_1_out, or_2_out);  // AND_Gate
endmodule

module c (
  input  [3:0] in_1,
  output c
);

  and and_1 (c, in_1[1], ~in_1[2], in_1[3]);  // AND_Gate
endmodule

module d (
  input  [3:0] in_1,
  output d
);

  wire or_1_out, or_2_out, or_3_out, or_4_out;

  or or_1 (or_1_out, ~in_1[1], ~in_1[3]);  // OR_Gate
  or or_2 (or_2_out, ~in_1[1], in_1[2]);  // OR_Gate
  or or_3 (or_3_out, in_1[2], ~in_1[3]);  // OR_Gate
  or or_4 (or_4_out, in_1[1], ~in_1[2], in_1[3]);  // OR_Gate
  and and_1 (d, in_1[0], or_1_out, or_2_out, or_3_out, or_4_out);
endmodule

module e (
  input  [3:0] in_1,
  output e
);

  wire or_1_out, or_2_out;

  or or_1 (or_1_out, ~in_1[1], ~in_1[3]);  // OR_Gate
  or or_2 (or_2_out, ~in_1[3], in_1[2]);  // OR_Gate
  and and_1 (e, or_1_out, or_2_out);
endmodule

module f (
  input  [3:0] in_1,
  output out_2
);

  wire or_1_out, or_2_out, or_3_out;

  or or_1 (or_1_out, in_1[1], ~in_1[2]);  // OR_Gate
  or or_2 (or_2_out, ~in_1[2], ~in_1[3]);  // OR_Gate
  or or_3 (or_3_out, in_1[1], ~in_1[3]);  // OR_Gate
  and and_1 (out_2, in_1[0], or_1_out, or_2_out, or_3_out);
endmodule

module g (
  input  [3:0] in_1,
  output g
);

  wire or_1_out, or_2_out, or_3_out;

  or or_1 (or_1_out, in_1[1], ~in_1[2]);  // OR_Gate
  or or_2 (or_2_out, ~in_1[1], in_1[2]);  // OR_Gate
  or or_3 (or_3_out, in_1[1], ~in_1[3]);  // OR_Gate
  and and_1 (g, in_1[0], or_1_out, or_2_out, or_3_out);
endmodule
