// Logisim project 17.circ as structural Verilog: 1 circuit, main circuit main
module main (
  input  A,
  input  B,
  input  C,
  input  D,
  output out_5
);

  wire and_1_out, and_2_out, and_3_out, and_4_out, and_5_out;

  and and_1 (and_1_out, ~A, ~B, C);  // AND_Gate
  and and_2 (and_2_out, ~A, B, D);  // AND_Gate
  and and_3 (and_3_out, B, ~C, D);  // AND_Gate
  and and_4 (and_4_out, A, ~C, D);  // AND_Gate
  and and_5 (and_5_out, A, ~B, C, D);  // AND_Gate
  or or_1 (out_5, and_1_out, and_2_out, and_3_out, and_4_out, and_5_out);

  // Notes on the sheet:
  //   'A'BC + 'ABD + B'CD + A'CD + A'BCD
endmodule
