// Logisim project 5.circ as structural Verilog: 1 circuit, main circuit main
module main (
  input  A,
  input  B,
  input  C,
  output [7:0] out_4
);

  wire and_1_out, and_2_out, and_3_out, and_4_out, and_5_out, and_6_out, and_7_out, and_8_out;

  and and_1 (and_1_out, ~A, ~B, ~C);  // AND_Gate
  and and_2 (and_2_out, ~A, ~B, C);  // AND_Gate
  and and_3 (and_3_out, ~A, B, ~C);  // AND_Gate
  and and_4 (and_4_out, ~A, B, C);  // AND_Gate
  and and_5 (and_5_out, A, ~B, ~C);  // AND_Gate
  and and_6 (and_6_out, A, ~B, C);  // AND_Gate
  and and_7 (and_7_out, A, B, ~C);  // AND_Gate
  and and_8 (and_8_out, A, B, C);
  or or_1 (out_4[0], and_4_out, and_5_out, and_7_out, and_8_out);
  or or_2 (out_4[1], and_2_out, and_4_out, and_6_out, and_8_out);
  or or_3 (out_4[3], and_1_out, and_2_out, and_4_out, and_5_out);
  or or_4 (out_4[2], and_1_out, and_4_out, and_6_out, and_7_out);
  or or_5 (out_4[4], and_3_out, and_5_out, and_7_out, and_8_out);
  or or_6 (out_4[5], and_2_out, and_3_out, and_6_out, and_8_out);
  or or_7 (out_4[6], and_1_out, and_3_out, and_6_out, and_7_out);
  or or_8 (out_4[7], and_1_out, and_2_out, and_3_out, and_5_out);
endmodule
