// Logisim project 6.circ as structural Verilog: 4 circuits, main circuit decodificador
module decodificador (
  input  [1:0] in_1,
  output out_2,
  output out_3,
  output out_4,
  output out_5
);

  and and_1 (out_2, ~in_1[0], ~in_1[1]);  // AND_Gate
  and and_2 (out_3, in_1[0], ~in_1[1]);  // AND_Gate
  and and_3 (out_4, ~in_1[0], in_1[1]);  // AND_Gate
  and and_4 (out_5, in_1[0], in_1[1]);
endmodule

module registrador (
  input  [7:0] in_1,
  input  clock,
  input  set,
  input  clear,
  output out_5,
  output out_6,
  output out_7,
  output out_8,
  output out_9,
  output out_10,
  output out_11,
  output out_12
);

  flipflopd flipflopd_1 (.in_1(set), .in_2(in_1[7]), .in_3(clock), .in_4(clear), .out_5(out_5));  // open: out_6
  flipflopd flipflopd_2 (.in_1(set), .in_2(in_1[6]), .in_3(clock), .in_4(clear), .out_5(out_6));  // open: out_6
  flipflopd flipflopd_3 (.in_1(set), .in_2(in_1[5]), .in_3(clock), .in_4(clear), .out_5(out_7));  // open: out_6
  flipflopd flipflopd_4 (.in_1(set), .in_2(in_1[4]), .in_3(clock), .in_4(clear), .out_5(out_8));  // open: out_6
  flipflopd flipflopd_5 (.in_1(set), .in_2(in_1[3]), .in_3(clock), .in_4(clear), .out_5(out_9));  // open: out_6
  flipflopd flipflopd_6 (.in_1(set), .in_2(in_1[2]), .in_3(clock), .in_4(clear), .out_5(out_10));  // open: out_6
  flipflopd flipflopd_7 (.in_1(set), .in_2(in_1[1]), .in_3(clock), .in_4(clear), .out_5(out_11));  // open: out_6
  flipflopd flipflopd_8 (.in_1(set), .in_2(in_1[0]), .in_3(clock), .in_4(clear), .out_5(out_12));  // open: out_6
endmodule

module flipflopd (
  input  in_1,
  input  in_2,
  input  in_3,
  input  in_4,
  output out_5,
  output out_6
);

  wire nand_1_out, nand_2_out, nand_3_out, nand_4_out, nand_5_out, nand_6_out, not_1_out, not_2_out,
       not_3_out;

  nand nand_1 (nand_1_out, in_2, in_3);
  nand nand_2 (nand_2_out, in_3, ~in_2);  // NAND_Gate
  not not_1 (not_1_out, in_3);
  nand nand_3 (nand_3_out, not_2_out, nand_1_out, nand_4_out);
  nand nand_4 (nand_4_out, nand_3_out, nand_2_out, not_3_out);
  not not_2 (not_2_out, in_1);
  nand nand_5 (nand_5_out, nand_3_out, not_3_out, not_1_out);
  nand nand_6 (nand_6_out, not_1_out, not_2_out, nand_4_out);
  not not_3 (not_3_out, in_4);
  nand nand_7 (out_5, nand_5_out, not_2_out, out_6);
  nand nand_8 (out_6, out_5, not_3_out, nand_6_out);
endmodule

module main (
  input  [7:0] in_1,
  input  [1:0] in_2,
  input  in_3,
  input  in_4,
  input  in_5,
  output [7:0] out_6
);

  wire and_1_out, and_2_out, and_3_out, and_4_out, decodificador_1_out_2, decodificador_1_out_3,
       decodificador_1_out_4, decodificador_1_out_5;
  wire [7:0] registrador_1_out_12, registrador_2_out_12, registrador_3_out_12, registrador_4_out_12;

  decodificador decodificador_1 (
    .in_1(in_2), .out_2(decodificador_1_out_2), .out_3(decodificador_1_out_3), .out_4(decodificador_1_out_4),
    .out_5(decodificador_1_out_5));
  and and_1 (and_1_out, decodificador_1_out_2, in_3);
  and and_2 (and_2_out, decodificador_1_out_3, in_3);
  and and_3 (and_3_out, decodificador_1_out_4, in_3);
  and and_4 (and_4_out, decodificador_1_out_5, in_3);
  registrador registrador_1 (
    .in_1(in_1), .clock(and_4_out), .set(in_4), .clear(in_5), .out_5(registrador_1_out_12[7]),
    .out_6(registrador_1_out_12[6]), .out_7(registrador_1_out_12[5]), .out_8(registrador_1_out_12[4]),
    .out_9(registrador_1_out_12[3]), .out_10(registrador_1_out_12[2]), .out_11(registrador_1_out_12[1]),
    .out_12(registrador_1_out_12[0]));
  registrador registrador_2 (
    .in_1(in_1), .clock(and_3_out), .set(in_4), .clear(in_5), .out_5(registrador_2_out_12[7]),
    .out_6(registrador_2_out_12[6]), .out_7(registrador_2_out_12[5]), .out_8(registrador_2_out_12[4]),
    .out_9(registrador_2_out_12[3]), .out_10(registrador_2_out_12[2]), .out_11(registrador_2_out_12[1]),
    .out_12(registrador_2_out_12[0]));
  assign out_6 = decodificador_1_out_5 ? registrador_1_out_12 : 8'bz;  // Controlled_Buffer controlled_buffer_1
  registrador registrador_3 (
    .in_1(in_1), .clock(and_2_out), .set(in_4), .clear(in_5), .out_5(registrador_3_out_12[7]),
    .out_6(registrador_3_out_12[6]), .out_7(registrador_3_out_12[5]), .out_8(registrador_3_out_12[4]),
    .out_9(registrador_3_out_12[3]), .out_10(registrador_3_out_12[2]), .out_11(registrador_3_out_12[1]),
    .out_12(registrador_3_out_12[0]));
  registrador registrador_4 (
    .in_1(in_1), .clock(and_1_out), .set(in_4), .clear(in_5), .out_5(registrador_4_out_12[7]),
    .out_6(registrador_4_out_12[6]), .out_7(registrador_4_out_12[5]), .out_8(registrador_4_out_12[4]),
    .out_9(registrador_4_out_12[3]), .out_10(registrador_4_out_12[2]), .out_11(registrador_4_out_12[1]),
    .out_12(registrador_4_out_12[0]));
  assign out_6 = decodificador_1_out_4 ? registrador_2_out_12 : 8'bz;  // Controlled_Buffer controlled_buffer_2
  assign out_6 = decodificador_1_out_3 ? registrador_3_out_12 : 8'bz;  // Controlled_Buffer controlled_buffer_3
  assign out_6 = decodificador_1_out_2 ? registrador_4_out_12 : 8'bz;  // Controlled_Buffer controlled_buffer_4
endmodule
